// Logisim project Unicycle Processor.circ as structural Verilog: 1 circuit, main circuit Processor
module Processor (
);

  wire alu_thirty_two_bits_1_zero, ALUSRC, and_1_out, CLK, control_unit_1_enrbwr, JR, MEMREAD, MEMWRITE;
  wire [1:0] ALUOP, JUMPOPT, RDOPT, WDOPT;
  wire [2:0] alu_controller_1_alu_op_2;
  wire [4:0] multiplexer_1_out;
  wire [27:0] shifter_1_out;
  wire [31:0] adder_1_out, adder_3_out, ALURESULT, bit_extender_1_out, DMDATA,
       instruction_memory_1_instruction, multiplexer_2_out, multiplexer_3_out, multiplexer_4_out,
       multiplexer_5_out, PC_8, PC_q, PCRESULT, register_bank_1_r1_2, shifter_2_out, WD;

  Clock clock_1 (.out(CLK));
  Register #(.width(32)) PC (.D(PCRESULT), .Q(PC_q), .clk(CLK));  // open: en, clr
  Adder #(.width(32)) adder_1 (.a(32'h4), .b(PC_q), .out(adder_1_out));  // open: cin, cout
  Adder #(.width(32)) adder_2 (.a(PC_q), .b(32'h8), .out(PC_8));  // open: cin, cout
  Instruction_Memory instruction_memory_1 (.PC_DIR(PC_q), .INSTRUCTION(instruction_memory_1_instruction));
  Shifter #(.width(28)) shifter_1 (.in(instruction_memory_1_instruction[27:0]), .\dist (5'b00010), .out(shifter_1_out));
  Control_Unit control_unit_1 (
    .OP(instruction_memory_1_instruction[31:26]), .RDOPT(RDOPT), .JUMPOPT(JUMPOPT), .MEMREAD(MEMREAD),
    .MEMWRITE(MEMWRITE), .WDPOPT(WDOPT), .ALUPOP(ALUOP), .ALUSRC(ALUSRC), .ENRBWR(control_unit_1_enrbwr));
  Multiplexer #(.select(2), .width(5)) multiplexer_1 (
    .in0(instruction_memory_1_instruction[20:16]), .in1(instruction_memory_1_instruction[15:11]),
    .in2({5{1'b1}}), .in3({5{1'b0}}), .out(multiplexer_1_out), .sel(RDOPT));  // open: en
  Multiplexer #(.select(2), .width(32)) multiplexer_2 (
    .in0(ALURESULT), .in1(DMDATA), .in2(PC_8), .in3({32{1'b0}}), .out(multiplexer_2_out), .sel(WDOPT));  // open: en
  Register_Bank register_bank_1 (
    .Clk(CLK), .R1(instruction_memory_1_instruction[25:21]), .R2(instruction_memory_1_instruction[20:16]),
    .WR(multiplexer_1_out), .WD(multiplexer_2_out), .ENWR(control_unit_1_enrbwr),
    .R1_2(register_bank_1_r1_2), .R2_2(WD));
  assign bit_extender_1_out = {{16{instruction_memory_1_instruction[15]}}, instruction_memory_1_instruction[15:0]};  // Bit_Extender bit_extender_1
  Shifter #(.width(32)) shifter_2 (.in(bit_extender_1_out), .\dist (5'b00010), .out(shifter_2_out));
  Multiplexer #(.width(32)) multiplexer_3 (
    .in0(WD), .in1(bit_extender_1_out), .out(multiplexer_3_out), .sel(ALUSRC));  // open: en
  ALU_Controller alu_controller_1 (
    .ALU_Op(ALUOP), .FUNCT(instruction_memory_1_instruction[5:0]), .JR(JR),
    .ALU_OP_2(alu_controller_1_alu_op_2));
  Adder #(.width(32)) adder_3 (.a(adder_1_out), .b(shifter_2_out), .out(adder_3_out));  // open: cin, cout
  and and_1 (and_1_out, JUMPOPT[0], JUMPOPT[1], alu_thirty_two_bits_1_zero);
  ALU_Thirty_Two_Bits alu_thirty_two_bits_1 (
    .RESULT(ALURESULT), .ALU_CODE(alu_controller_1_alu_op_2), .R2(multiplexer_3_out), .CIN(1'b0),
    .R1(register_bank_1_r1_2), .ZERO(alu_thirty_two_bits_1_zero));
  Multiplexer #(.width(32)) multiplexer_4 (.in0(adder_1_out), .out(multiplexer_4_out), .sel(JR));  // open: in1, en
  Multiplexer #(.width(32)) multiplexer_5 (
    .in0(adder_1_out), .in1(adder_3_out), .out(multiplexer_5_out), .sel(and_1_out));  // open: en
  // Data_Memory data_memory_1: pin names not known; wires that end beside it: ALURESULT, CLK, WD, MEMWRITE, MEMREAD, DMDATA
  Multiplexer #(.select(2), .width(32)) multiplexer_6 (
    .in0({adder_1_out[31:28], shifter_1_out}), .in1({adder_1_out[31:28], shifter_1_out}),
    .in2(multiplexer_4_out), .in3(multiplexer_5_out), .out(PCRESULT), .sel(JUMPOPT));  // open: en
endmodule
